# Fritzing sketch schematic (saved by Fritzing 0.9.3b)
breadboards: 1

parts:
  M1 = STM32F103C8T6 blue mini board
  U1 = ESP8266 WiFi Module [part_number=ESP8266]
  DHT1 = Humidity and Temperature Sensor DHT11
  R1 = Resistor [tolerance=±5% resistance=10k package="0805 [SMD]"]
  R2 = Resistor [tolerance=±5% resistance=10k package="0805 [SMD]"]

nets:
  N1: M1.A9, U1.RXD
  N2: M1.A10, U1.TXD
  N3: M1.B6, DHT1.Data-signal, R1.Pin_1
  GND: M1.G, M1.GND, U1.GND, DHT1.GND_2
  VCC: M1.3.3V, U1.VCC, DHT1.Vcc, R1.Pin_0, R2.Pin_0
  N4: U1.CH_PD, R2.Pin_1

custom parts:
  ESP8266 WiFi Module: Generic WiFi Module based on the ESP8266 with onboard PCB antenna and UART communications
  Humidity and Temperature Sensor DHT11: Digital relative humidity & temperature sensor DHT11
