# Fritzing sketch f103_conn (saved by Fritzing 0.9.3b)
breadboards: 1

parts:
  U1 = POT [package=pot_mammoth]
  M1 = STM32F103C8T6 blue mini board
  LED1 = LED - 3mm [color="Blue (430nm)" package="3 mm [THT]"]
  R1 = Resistor [tolerance=±5% resistance=220 package="2010 [SMD]"]
  LED2 = LED - 3mm [color="Red (633nm)" package="3 mm [THT]"]
  R2 = Resistor [tolerance=±5% resistance=220 package="2010 [SMD]"]
  LED3 = LED - 3mm [color="Red (633nm)" package="3 mm [THT]"]
  R3 = Resistor [tolerance=±5% resistance=220 package="2010 [SMD]"]
  JP1 = Header 4 [package=screwterminal-3.5mm-4_lock]

nets:
  N1: U1.S, M1.3.3V
  N2: U1.A, M1.A0
  N3: U1.E, M1.G, M1.GND, LED1.cathode, LED2.cathode, LED3.cathode, JP1.4
  N4: M1.A9, JP1.3
  N5: M1.A10, JP1.2
  N6: M1.5V, JP1.1
  N7: M1.B0, R1.Pin_1
  N8: M1.B1, R2.Pin_1
  N9: M1.B10, R3.Pin_1
  N10: LED1.anode, R1.Pin_0
  N11: LED2.anode, R2.Pin_0
  N12: LED3.anode, R3.Pin_0

notes:
  NEXTION 3,5"
  5V TX RX GND
