# Fritzing sketch f103_tcp_server_1 (saved by Fritzing 0.9.3b)
breadboards: 1

parts:
  M1 = STM32F103C8T6 blue mini board
  LED1 = LED - 3mm [color="Red (633nm)" package="3 mm [THT]"]
  LED2 = LED - 3mm [color="Red (633nm)" package="3 mm [THT]"]
  LED3 = LED - 3mm [color="Red (633nm)" package="3 mm [THT]"]
  Componente3 = ENC28J60 Breakout Board
  S1 = Momentary Switch [package=ksa_sealed_tac_switch]
  R1 = Resistor [tolerance=±5% resistance=220 package="2010 [SMD]"]
  R2 = Resistor [tolerance=±5% resistance=220 package="2010 [SMD]"]
  R3 = Resistor [tolerance=±5% resistance=220 package="2010 [SMD]"]
  R4 = Rotary Potentiometer (Large) [maximum_resistance=100kΩ package=THT]
  R5 = Rotary Potentiometer (Large) [maximum_resistance=100kΩ package=THT]
  Parça1 = FTDI Basic Programmer

nets:
  N1: M1.B12, LED1.anode
  N2: M1.B13, LED2.anode
  N3: M1.B14, LED3.anode
  N4: M1.B15, S1.3
  N5: M1.A8, Componente3.RESET
  N6: M1.A15, Componente3.CS
  N7: M1.B3, Componente3.SCK
  N8: M1.B4, Componente3.SO
  N9: M1.B5, Componente3.SI
  GND: M1.G, M1.GND, Componente3.GND, S1.2, R1.Pin_1, R2.Pin_1, R3.Pin_1, R4.leg1, R5.leg1, Parça1.GND
  3.3V: M1.3.3V, Componente3.VCC, R4.leg2, R5.leg2
  N10: M1.B10, Parça1.RXI
  N11: M1.B11, Parça1.TXO
  N12: LED1.cathode, R1.Pin_0
  N13: LED2.cathode, R2.Pin_0
  N14: LED3.cathode, R3.Pin_0

custom parts:
  ENC28J60 Breakout Board: This is a breakout board for the Microchip ENC28J60 stand-alone ethernet controller. The ENC28J60 has an SPI interface. It operates at 3.3 Volts.
